# Fritzing sketch liedetector (saved by Fritzing 0.9.6b)
circuit board: 13.9503cm x 8.07273cm

parts:
  R1 = Resistor [tolerance=±5% power=0.25 resistance=4.7k package=THT]
  R2 = Resistor [tolerance=±5% power=0.25 resistance=82k package=THT]
  C1 = Tantalum Capacitor [capacitance=1pF voltage=6.3V package="100 mil [THT, tantalum]"]
  Q1 = PNP-Transistor [part_number=2N3906 package="TO92 [THT]"]
  U1 = SWITCH-SPST-2 [package=r_sw_th]
  SP1 = SPEAKER [package=pcb_mount_speaker]
  SJ1 = Solder Jumper [package=sj_2s]
  Q2 = NPN-Transistor [part_number=2N3904 package="TO92 [THT]"]
  VCC1 = Battery block 9V

nets:
  N1: R1.Pin_0, Q2.B
  N2: R1.Pin_1, R2.Pin_1, C1.+, SJ1.1, SJ1.2
  N3: R2.Pin_0, Q1.B, Q2.C
  N4: C1.-, Q1.C, SP1.+
  N5: Q1.E, VCC1.-
  N6: U1.O, SP1.-, Q2.E
  N7: U1.P, VCC1.+
