# Fritzing sketch moter cycle hed light (saved by Fritzing 0.9.6b)
breadboards: 1

parts:
  D1 = Rectifier Diode 10A [part_number=P1000K]
  U1 = TRANSISTOR_NPN_2 [package=to-92]
  D2 = Rectifier Diode [part_number=1N4001 package="300 mil [THT]"]
  Fuse1 = Fuse with Handler [part_number=15A]
  Q1 = PNP-Transistor [package="TO92 [THT]"]
  BAT1 = BC9VPC [package=bc9vpc]
  U2 = LCD_BACKLIGHT_PADS [package=lcd_backlight_pads]
  R5 = TRIMPOT [package=trimpot-3mm-2]
  R3 = Resistor [tolerance=±5% resistance=22 power=5W package="2010 [SMD]"]
  R2 = Resistor [tolerance=±5% resistance=1 power=1W package="2512 [SMD]"]
  R4 = Resistor [tolerance=±5% resistance=22 power=5W package="1206 [SMD]"]
  R1 = Resistor [tolerance=±5% resistance=22 power=5W package="1206 [SMD]"]

nets:
  N1: D1.cathode, R2.Pin_0, R1.Pin_1
  N2: D1.anode, U1.E, BAT1.V-, U2.A
  N3: U1.C, R4.Pin_1
  N4: U1.B, D2.anode
  N5: D2.cathode, R3.Pin_1
  N6: Fuse1.Connector1, BAT1.V+
  N7: Fuse1.Connector2, Q1.E, R1.Pin_0
  N8: Q1.B, R5.WIPER
  N9: Q1.C, U2.K, R3.Pin_0
  N10: R5.CCW, R2.Pin_1
  N11: R5.CW, R4.Pin_0
